# Fritzing sketch Doggy feeded (saved by Fritzing 0.9.9b)

parts:
  Arduino_NANO = Arduino Nano (Rev3.0)
  Pet_is_FED = Waterproof Pushbutton (green)
  BUTTON2 = Waterproof Pushbutton (green)
  Pet_is_HUNGRY = LED - 3mm [color="Red (633nm)" current=0.030 package="3 mm [THT]"]
  LED2 = LED - 3mm [color="Red (633nm)" current=0.030 package="3 mm [THT]"]
  R1 = Resistor [tolerance=±5% power=0.25 resistance=220 package=THT]
  R2 = Resistor [tolerance=±5% power=0.25 resistance=220 package=THT]
  R3 = Resistor [tolerance=±5% power=0.25 resistance=220 package=THT]
  R4 = Resistor [tolerance=±5% power=0.25 resistance=220 package=THT]

nets:
  N1: Arduino_NANO.GND, Pet_is_FED.no_name_yet#1, Pet_is_FED.no_name_yet#5, BUTTON2.no_name_yet#1, BUTTON2.no_name_yet#5, Pet_is_HUNGRY.cathode, LED2.cathode
  N2: Arduino_NANO.D2, R3.Pin_1
  N3: Arduino_NANO.D3, R2.Pin_1
  N4: Arduino_NANO.D4, R4.Pin_1
  N5: Arduino_NANO.D5, R1.Pin_1
  N6: Arduino_NANO.D7, BUTTON2.no_name_yet#2
  N7: Arduino_NANO.D8, Pet_is_FED.no_name_yet#2
  N8: Pet_is_FED.no_name_yet#4, R4.Pin_0
  N9: BUTTON2.no_name_yet#4, R3.Pin_0
  N10: Pet_is_HUNGRY.anode, R1.Pin_0
  N11: LED2.anode, R2.Pin_0

notes:
  AM
  PM

custom parts:
  Waterproof Pushbutton (green): Waterproof Illuminated Pushbutton (green)
